# Fritzing sketch wiringguide (saved by Fritzing 0.9.3b)
breadboards: 1

parts:
  Mega_2560 = Arduino Mega 2560 (Rev3)
  female_RJ45_Team_A = RJ45 Jack [package=rj45-8]
  C1 = Ceramic Capacitor [capacitance=100nF package="100 mil [THT, multilayer]"]
  male_RJ45_Team_A = RJ45 Jack [package=rj45-8]
  A1 = Square Pushbutton
  A2 = Square Pushbutton
  A3 = Square Pushbutton
  A4 = Square Pushbutton
  LCD1 = LCD screen
  R1 = Resistor [tolerance=±5% resistance=2.2k package=THT]
  R2 = Resistor [tolerance=±5% resistance=1k package=THT]
  2N3904 = NPN-Transistor [package="TO92 [THT]"]
  R3 = Resistor [tolerance=±5% resistance=100 package=THT]
  Clear = Square Pushbutton
  Mode = Toggle Switch [package=THT]
  SPKR1 = Loudspeaker

nets:
  GND: Mega_2560.GND, female_RJ45_Team_A.2, C1.0, LCD1.VSS, LCD1.R/W, LCD1.LED-, R1.Pin_1, 2N3904.E, Clear.leg1, Mode.L2
  N1: Mega_2560.D9_PWM, R2.Pin_0
  5V: Mega_2560.5V, LCD1.VDD, LCD1.LED+, SPKR1.pin1
  N2: Mega_2560.D3_PWM, Mode.COM
  N3: Mega_2560.D28, Clear.leg0
  N4: Mega_2560.D30, female_RJ45_Team_A.1, C1.1
  N5: Mega_2560.D42, LCD1.DB7
  N6: Mega_2560.D43, LCD1.DB6
  N7: Mega_2560.D44, LCD1.DB5
  N8: Mega_2560.D45, LCD1.DB4
  N9: Mega_2560.D46, LCD1.DB3
  N10: Mega_2560.D47, LCD1.DB2
  N11: Mega_2560.D48, LCD1.DB1
  N12: Mega_2560.D49, LCD1.DB0
  N13: Mega_2560.D50, LCD1.E
  N14: Mega_2560.D51, LCD1.RS
  N15: male_RJ45_Team_A.1, A1.leg1
  N16: male_RJ45_Team_A.2, A1.leg0
  N17: male_RJ45_Team_A.3, A2.leg1
  N18: male_RJ45_Team_A.4, A2.leg0
  N19: male_RJ45_Team_A.5, A3.leg1
  N20: male_RJ45_Team_A.6, A3.leg0
  N21: male_RJ45_Team_A.7, A4.leg1
  N22: male_RJ45_Team_A.8, A4.leg0
  N23: LCD1.V0, R1.Pin_0
  N24: R2.Pin_1, 2N3904.B
  N25: 2N3904.C, R3.Pin_0
  N26: R3.Pin_1, SPKR1.pin2

notes:
  Team A female RJ45:
  RJ45 1,3,5,7 to D30,D31,D32,D33
  RJ45 2,4,6,8 to GND
  Team B female RJ45:
  RJ45 1,3,5,7 to D34,D35,D36,D37
  RJ45 2,4,6,8 to GND
  Team C female RJ45
  RJ45 1,3,5,7 to D38,D39,D40,D41
  RJ45 2,4,6,8 to GND
  100nF capacitors
  between 1 and 2, 3 and 6, 4 and 5, and 7 and 8 on all female RJ45s
  repeat for teams B and C
  need 220R
  resistor between LED+ and 5V if screen doesn't supply
